# Fritzing sketch fotobox_shield (saved by Fritzing 0.8.3b)

parts:
  Part1 = Arduino Prototyping Shield
  J1 = female pin header, 8 pins [form="♀ (female)"]
  U1 = TLP621 [package=THT]
  U2 = TLP621 [package=THT]
  U3 = TLP621 [package=THT]
  U4 = TLP621 [package=THT]
  J2 = female pin header, 8 pins [form="♀ (female)"]

nets:
  N1: Part1.+5V, Part1.N$393, J1.pin7
  N2: Part1.GND, Part1.N$117, J1.pin8
  N3: Part1.D2, Part1.N$427, J1.pin1
  N4: Part1.D3, Part1.N$425, J1.pin2
  N5: Part1.D4, Part1.N$405, J1.pin3
  N6: Part1.D5, Part1.N$403, J1.pin4
  N7: Part1.D6, Part1.N$398, J1.pin5
  N8: Part1.D7, Part1.N$396, J1.pin6
  N9: Part1.A1, Part1.N$275, U1.Pin_1
  N10: Part1.N$43, J2.pin1
  N11: Part1.N$51, J2.pin2
  N12: Part1.N$81, J2.pin5
  N13: Part1.N$274, U1.Pin_2
  N14: Part1.N$285, U2.Pin_1
  N15: Part1.N$289, U2.Pin_2
  N16: Part1.N$293, U1.Pin_4
  N17: Part1.N$327, J2.pin7
  N18: Part1.N$354, J2.pin8
  N19: Part1.N$355, U4.Pin_3
  N20: Part1.N$358, U4.Pin_2
  N21: Part1.N$359, U2.Pin_3
  N22: Part1.N$363, U2.Pin_4
  N23: Part1.N$365, U4.Pin_1
  N24: Part1.N$366, U4.Pin_4
  N25: Part1.N$369, J2.pin6
  N26: Part1.N$370, U3.Pin_3
  N27: Part1.N$373, U3.Pin_2
  N28: Part1.N$375, U1.Pin_3
  N29: Part1.N$376, U3.Pin_1
  N30: Part1.N$379, U3.Pin_4
  N31: Part1.N$380, J2.pin4
  N32: Part1.N$383, J2.pin3
