# Fritzing sketch lcd board (saved by Fritzing 0.8.0b)
stripboards: 1

parts:
  J1 = female pin header, 6 pins [form="♀ (female)"]
  J2 = female pin header, 6 pins [form="♀ (female)"]
  J3 = female pin header, 8 pins [form="♀ (female)"]
  R2 = Trimmer Potentiometer [maximum_resistance=10kΩ package=THT]
  LCD1 = LCD screen

nets:
  N1: J1.pin1, R2.leg1, LCD1.VSS
  N2: J1.pin2, J1.pin5, J2.pin5, J2.pin6, J3.pin7, J3.pin8, R2.leg2, LCD1.VDD, LCD1.R/W, LCD1.LED+, LCD1.LED-
  N3: J1.pin3, R2.wiper, LCD1.V0
  N4: J1.pin4, J3.pin1, LCD1.RS
  N5: J1.pin6, J3.pin2, LCD1.E
  N6: J2.pin1, J3.pin3, LCD1.DB4
  N7: J2.pin2, J3.pin4, LCD1.DB5
  N8: J2.pin3, J3.pin5, LCD1.DB6
  N9: J2.pin4, J3.pin6, LCD1.DB7
